# Fritzing sketch onokairo_bord_v7 (saved by Fritzing 0.9.5d)
breadboards: 1

parts:
  Mod1 = Raspberry Pi 4B
  DS1 = DS18B20 1-Wire Temperature Sensor [part_number=DS18B20]
  S1 = Pushbutton [package=THT]
  S2 = Pushbutton [package="[THT]"]
  R2 = Resistor [tolerance=±5% resistance=330 package=THT]
  LED1 = LED - 3mm [color="Red (633nm)" package="3 mm [THT]"]
  MCP1 = MCP3208
  パーツ1 = Adafruit SCD4x [part_number="Adafruit #5187"]
  R1 = Resistor [tolerance=±5% resistance=10k package=THT]
  R4 = Resistor [tolerance=±5% resistance=10k package=THT]
  IC1 = IC, DIP package, 8 pins [chip_label=IC]
  R9 = Resistor [tolerance=±5% resistance=510k package=THT]
  R5 = Photocell (LDR) [package=THT]
  R12 = Resistor [tolerance=±5% resistance=510k package=THT]
  R13 = 1k Ω Resistor [package=THT]
  R14 = 1k Ω Resistor [package=THT]

nets (from the breadboard view):
  VDD: Mod1.3V3, DS1.VDD, S1.leg1, S2.Pin_3, S2.Pin_4, MCP1.Chan_2, MCP1.VREF, MCP1.VDD, パーツ1.VCC, R1.Pin_1, IC1.pin8, R5.pin_0
  N1: Mod1.GPIO2, パーツ1.SCL
  N2: Mod1.GPIO3, パーツ1.SDA
  GND: Mod1.GND, DS1.GND, LED1.cathode, MCP1.DGND, MCP1.AGND, パーツ1.GND, R4.Pin_1, IC1.pin4, R13.Pin_1, R14.Pin_1
  N3: Mod1.GPIO4, DS1.DQ, R1.Pin_0
  N4: Mod1.GPIO10, MCP1.DIN
  N5: Mod1.GPIO9, MCP1.DOUT
  N6: Mod1.GPIO11, MCP1.CLK
  N7: Mod1.GPIO8, MCP1.CS/SHDN
  N8: Mod1.GPIO16, R2.Pin_1
  N9: Mod1.GPIO20, S2.Pin_1, S2.Pin_2
  N10: Mod1.GPIO21, S1.leg0
  N11: R2.Pin_0, LED1.anode
  N12: MCP1.Chan_0, IC1.pin1, R12.Pin_0
  N13: MCP1.Chan_1, IC1.pin7, R9.Pin_0
  N14: R4.Pin_0, R5.pin_1
  N15: IC1.pin2, R12.Pin_1, R13.Pin_0
  N16: IC1.pin6, R9.Pin_1, R14.Pin_0

notes:
  ECセンサ
  MCP6002
  （IC）
  pHセンサ
  EC
  MCP6002
  pH

custom parts:
  Adafruit SCD4x: Take a deep breath in...now slowly breathe out. Mmm isn't it wonderful? All that air around us, which we bring into our lungs, extracts oxygen from and then breathes out carbon dioxide. CO2 is essential for life on this planet we call Earth - we and plants take turns using and emitting CO2 in an elegant symbiosis. But it's important to keep that CO2 balanced - you don't want too much around,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
  1k Ω Resistor: A generic resistor (0.25W)
